# Fritzing sketch RelaySchema (saved by Fritzing 0.9.3b)

parts:
  U1 = 4-Channel 5v Relay Shield [package=relay-4ch5v10a]
  Součástka1 = Arduino Uno (Rev3)

nets:
  VCC: U1.VCC, Součástka1.5V
  GND: U1.GND, Součástka1.GND
  N1: U1.IN1, Součástka1.D13/SCK
  N2: U1.IN2, Součástka1.D12/MISO
  N3: U1.IN4, Součástka1.D10_PWM/SS
  N4: U1.IN3, Součástka1.D11_PWM/MOSI

custom parts:
  4-Channel 5v Relay Shield: 4 Channel 5v Relay Shield w. 2x SPD-06VDC-SD-C
