# Fritzing sketch CO senzor oxidu uhelnatého (saved by Fritzing 0.9.3b)
breadboards: 1

parts:
  Součástka2 = Arduino Uno (Rev3)
  TM1638_Led_and_Key2 = TM1638_Led_and_Key [package=THT]
  J1 = female pin header, 2 pins [form="♀ (female)"]
  J2 = female pin header, 2 pins [form="♀ (female)"]

nets:
  N1: Součástka2.A2, J1.pin1
  N2: Součástka2.D8, TM1638_Led_and_Key2.CLK
  N3: Součástka2.D9_PWM, TM1638_Led_and_Key2.STB
  N4: Součástka2.D4, J1.pin2
  N5: Součástka2.D7, TM1638_Led_and_Key2.DIO
  5V: Součástka2.5V, TM1638_Led_and_Key2.VCC, J2.pin2
  GND: Součástka2.GND, TM1638_Led_and_Key2.GND, J2.pin1

notes:
  GND
  +5V
  AO
  DO
