# Fritzing sketch KY-013 (saved by Fritzing 0.9.3b)
breadboards: 1

parts:
  Součástka1 = Arduino Uno (Rev3)
  Part1 = KY-013 Analog Temperature Sensor Module [package="Breakout board"]

nets:
  N1: Součástka1.A0, Part1.Vin
  N2: Součástka1.5V, Part1.S
  N3: Součástka1.GND, Part1.-

custom parts:
  KY-013 Analog Temperature Sensor Module: KY-013 Analog Temperature Sensor module, measures ambient temperature based on resistance of the thermistor.
